// Logisim project cpu.circ as structural Verilog: 2 circuits, main circuit main
module main (
  input  [31:0] INSTRUCTION,
  input  CLOCK,
  output [31:0] PROGRAM_COUNTER,
  output [31:0] ra,
  output [31:0] sp,
  output [31:0] t0,
  output [31:0] t1,
  output [31:0] t2,
  output [31:0] s0,
  output [31:0] s1,
  output [31:0] a0
);

  wire DMEM_p1, DMEM_p3, DMEM_p5;
  wire [2:0] funct3;
  wire [4:0] rd, rs1;
  wire [6:0] opcode;
  wire [11:0] imm;
  wire [31:0] adder_1_out, Arithmetic_Logic_Unit_result, immgen_1_out_3, multiplexer_1_out,
       RegFile_read_data_1, RegFile_read_data_2;

  Adder #(.width(32)) adder_1 (.a(PROGRAM_COUNTER), .b(32'h4), .out(adder_1_out));  // open: cin, cout
  Register #(.width(32)) register_1 (
    .D(INSTRUCTION), .clk(CLOCK), .Q({imm, rs1, funct3, rd, opcode}));  // open: en, clr
  Register #(.width(32)) PC (.D(adder_1_out), .clk(CLOCK), .Q(PROGRAM_COUNTER));  // open: en, clr
  ImmGen immgen_1 (.in_1(1'b1), .in_2(imm), .out_3(immgen_1_out_3));
  regfile_main RegFile (
    .rs2(imm[4:0]), .rd(rd), .Read_Data_1(RegFile_read_data_1), .Read_Data_2(RegFile_read_data_2), .ra(ra),
    .sp(sp), .t0(t0), .t1(t1), .t2(t2), .s0(s0), .s1(s1), .a0(a0), .rs1(rs1),
    .Write_Data(Arithmetic_Logic_Unit_result), .RegWEn(1'b1), .clk(CLOCK));
  Multiplexer #(.width(32), .enable("false")) multiplexer_1 (
    .in0(RegFile_read_data_2), .in1(immgen_1_out_3), .out(multiplexer_1_out), .sel(1'b1));
  alu Arithmetic_Logic_Unit (
    .B(multiplexer_1_out), .Result(Arithmetic_Logic_Unit_result), .A(RegFile_read_data_1), .ALUSel(4'b0000));
  // mem_main DMEM: pin names not known; wires that end beside it: DMEM_p1, DMEM_p1, DMEM_p3, DMEM_p3, DMEM_p5

  // Other names for the same wires on the sheet: rs2[4:0] = imm[4:0]; clk = CLOCK

  // Notes on the sheet:
  //   Output
  //   IMEM (do **NOT** move this)
  //   Inputs
  //   Inputs/Outputs for testing. Do **NOT** move these.
endmodule

module ImmGen (
  input  in_1,
  input  [11:0] in_2,
  output [31:0] out_3
);

  wire bitselector_1_out;
  wire [31:0] and_1_out, bit_extender_1_out;

  BitSelector #(.width(12)) bitselector_1 (.in(in_2), .out(bitselector_1_out), .sel(4'b1011));
  assign bit_extender_1_out = {{20{in_2[11]}}, in_2};  // Bit_Extender bit_extender_1
  Multiplexer #(.width(32), .enable("false")) multiplexer_1 (
    .in0(bit_extender_1_out), .in1(and_1_out), .out(out_3), .sel(bitselector_1_out));
  assign and_1_out = {32{1'b1}} & bit_extender_1_out;  // AND_Gate and_1, 32 bits wide
endmodule
